// Logisim project jk_circ.circ as structural Verilog: 1 circuit, main circuit main
module main (
  input  Reset,
  input  [3:0] Entrada_1,
  input  [3:0] Entrada_2,
  input  Sel_AB,
  input  Sel_C
);

  wire Clock_out;
  wire [3:0] multiplexer_1_out, multiplexer_2_out, multiplexer_3_out, Reg_A_q, Reg_B_q, Reg_C_q, Soma_p3,
       Subtracao_p3;

  Clock Clock (.out(Clock_out));
  Multiplexer #(.width(4), .enable("false")) multiplexer_1 (
    .in0(Reg_C_q), .in1(Entrada_1), .out(multiplexer_1_out), .sel(Sel_AB));
  Multiplexer #(.width(4), .enable("false")) multiplexer_2 (
    .in0(Reg_A_q), .in1(Entrada_2), .out(multiplexer_2_out), .sel(Sel_AB));
  Register #(.width(4)) Reg_A (.D(multiplexer_1_out), .Q(Reg_A_q), .clk(Clock_out), .clr(Reset));  // open: en
  Register #(.width(4)) Reg_B (.D(multiplexer_2_out), .Q(Reg_B_q), .clk(Clock_out), .clr(Reset));  // open: en
  // Somatorio_main Soma: pin names not known; wires that end beside it: Reg_A_q, Reg_B_q, Soma_p3
  // Subtrator_main Subtracao: pin names not known; wires that end beside it: Reg_A_q, Reg_B_q, Subtracao_p3
  Multiplexer #(.width(4), .enable("false")) multiplexer_3 (
    .in0(Soma_p3), .in1(Subtracao_p3), .out(multiplexer_3_out), .sel(Sel_C));
  Register #(.width(4)) Reg_C (.D(multiplexer_3_out), .Q(Reg_C_q), .clk(Clock_out), .clr(Reset));  // open: en

  // Notes on the sheet:
  //   0 = add e 1 = sub
endmodule
